# Fritzing sketch Layout (saved by Fritzing 0.9.2b)

parts:
  Arduino_Uno = Arduino Uno (Rev3)
  R1 = Rotary Potentiometer (Small) [maximum_resistance=100kΩ package=THT]
  R2 = Rotary Potentiometer (Small) [maximum_resistance=100kΩ package=THT]
  M1 = DC Motor  # not connected
  M2 = DC Motor  # not connected

nets:
  N1: Arduino_Uno.A0, R1.wiper
  N2: Arduino_Uno.A1, R2.wiper
  N3: Arduino_Uno.5V, R1.leg2, R2.leg2
  N4: Arduino_Uno.GND, R1.leg1, R2.leg1

notes:
  The Motor Shield is not included in this drawing due to technical limitations of this software. It will stack directly on top of the arduino using the header pins.
  I would recommend using a 12 V Battery to power everything. This would be input to the power jack on the arduino, as well as split to the power input connection on the motor shield board. Make sure to remove the jumper J2 on the motor shield.
